// Logisim project counter.circ as structural Verilog: 3 circuits, main circuit main
module main (
  input  C,
  output A3,
  output A2,
  output A1,
  output A0
);

  wire and_1_out, nand_1_out, nand_2_out, nand_3_out, nand_4_out;

  nand nand_1 (nand_1_out, 1'b1, and_1_out);
  JK jk_1 (.J(nand_1_out), .C(C), .K(1'b1), .CLR(and_1_out), .Q(A0));  // open: PR, nQ
  nand nand_2 (nand_2_out, 1'b1, and_1_out);
  JK jk_2 (.J(nand_2_out), .C(A0), .K(1'b1), .CLR(and_1_out), .Q(A1));  // open: PR, nQ
  nand nand_3 (nand_3_out, 1'b1, and_1_out);
  JK jk_3 (.J(nand_3_out), .C(A1), .K(1'b1), .CLR(and_1_out), .Q(A2));  // open: PR, nQ
  nand nand_4 (nand_4_out, 1'b1, and_1_out);
  JK jk_4 (.J(nand_4_out), .C(A2), .K(1'b1), .CLR(and_1_out), .Q(A3));  // open: PR, nQ
  and and_1 (and_1_out, A3, ~A2, A1, ~A0);  // AND_Gate
endmodule

module RS (
  input  PR,
  input  S,
  input  C,
  input  R,
  input  CLR,
  output Q,
  output nQ
);

  wire nand_1_out, nand_2_out, por_1_out;

  nand nand_1 (nand_1_out, S, C);
  nand nand_2 (nand_2_out, C, R);
  POR por_1 (.out(por_1_out));
  nand nand_3 (Q, ~PR, nand_1_out, nQ);  // NAND_Gate
  nand nand_4 (nQ, Q, nand_2_out, ~CLR, ~por_1_out);  // NAND_Gate
endmodule

module JK (
  input  PR,
  input  J,
  input  C,
  input  K,
  input  CLR,
  output Q,
  output nQ
);

  wire and_1_out, and_2_out, not_1_out, rs_1_nq, rs_1_q;

  and and_1 (and_1_out, nQ, J);
  and and_2 (and_2_out, K, Q);
  not not_1 (not_1_out, C);
  RS rs_1 (.PR(PR), .S(and_1_out), .C(C), .R(and_2_out), .CLR(CLR), .Q(rs_1_q), .nQ(rs_1_nq));
  RS rs_2 (.PR(PR), .S(rs_1_q), .C(not_1_out), .R(rs_1_nq), .CLR(CLR), .Q(Q), .nQ(nQ));
endmodule
