// Logisim project lfsr.circ as structural Verilog: 3 circuits, main circuit main
module main (
  input  in_1,
  output A11,
  output A10,
  output A9,
  output A8,
  output A7,
  output A6,
  output A5,
  output A4,
  output A3,
  output A2,
  output A1,
  output A0
);

  wire not_1_out, not_2_out, not_3_out, not_4_out, por_1_out, S2_nq, S5_nq, S6_nq, S7_nq, S7_q, S8_nq, S9_nq,
       S10_nq, S11_nq, S12_nq, xor_1_out, xor_2_out, xor_3_out;

  JK S6 (.J(S7_q), .C(in_1), .K(S7_nq), .Q(A6), .nQ(S6_nq));  // open: PR, CLR
  not not_1 (not_1_out, A0);
  JK S12 (.J(A0), .C(in_1), .K(not_1_out), .Q(A11), .nQ(S12_nq));  // open: PR, CLR
  JK S5 (.J(A6), .C(in_1), .K(S6_nq), .Q(A5), .nQ(S5_nq));  // open: PR, CLR
  JK S11 (.J(A11), .C(in_1), .K(S12_nq), .Q(A10), .nQ(S11_nq));  // open: PR, CLR
  JK S4 (.J(A5), .C(in_1), .K(S5_nq), .Q(A4));  // open: PR, CLR, nQ
  xor xor_1 (xor_1_out, A4, A0);
  not not_2 (not_2_out, xor_1_out);
  JK S10 (.J(A10), .C(in_1), .K(S11_nq), .Q(A9), .nQ(S10_nq));  // open: PR, CLR
  JK S3 (.J(xor_1_out), .C(in_1), .K(not_2_out), .Q(A3));  // open: PR, CLR, nQ
  xor xor_2 (xor_2_out, A3, A0);
  not not_3 (not_3_out, xor_2_out);
  JK S9 (.J(A9), .C(in_1), .K(S10_nq), .Q(A8), .nQ(S9_nq));  // open: PR, CLR
  JK S2 (.J(xor_2_out), .C(in_1), .K(not_3_out), .Q(A2), .nQ(S2_nq));  // open: PR, CLR
  JK S8 (.J(A8), .C(in_1), .K(S9_nq), .Q(A7), .nQ(S8_nq));  // open: PR, CLR
  JK S1 (.J(A2), .C(in_1), .K(S2_nq), .Q(A1));  // open: PR, CLR, nQ
  POR por_1 (.out(por_1_out));
  xor xor_3 (xor_3_out, A1, A0);
  not not_4 (not_4_out, xor_3_out);
  JK S7 (.J(A7), .C(in_1), .K(S8_nq), .Q(S7_q), .nQ(S7_nq));  // open: PR, CLR
  JK S0 (.PR(por_1_out), .J(xor_3_out), .C(in_1), .K(not_4_out), .Q(A0));  // open: CLR, nQ
endmodule

module RS (
  input  PR,
  input  S,
  input  C,
  input  R,
  input  CLR,
  output Q,
  output nQ
);

  wire nand_1_out, nand_2_out, por_1_out;

  nand nand_1 (nand_1_out, S, C);
  nand nand_2 (nand_2_out, C, R);
  POR #(.PorHighDuration(1)) por_1 (.out(por_1_out));
  nand nand_3 (Q, ~PR, nand_1_out, nQ);  // NAND_Gate
  nand nand_4 (nQ, Q, nand_2_out, ~CLR, ~por_1_out);  // NAND_Gate
endmodule

module JK (
  input  PR,
  input  J,
  input  C,
  input  K,
  input  CLR,
  output Q,
  output nQ
);

  wire and_1_out, and_2_out, not_1_out, rs_1_nq, rs_1_q;

  and and_1 (and_1_out, nQ, J);
  and and_2 (and_2_out, K, Q);
  not not_1 (not_1_out, C);
  RS rs_1 (.PR(PR), .S(and_1_out), .C(C), .R(and_2_out), .CLR(CLR), .Q(rs_1_q), .nQ(rs_1_nq));
  RS rs_2 (.PR(PR), .S(rs_1_q), .C(not_1_out), .R(rs_1_nq), .CLR(CLR), .Q(Q), .nQ(nQ));
endmodule
